# Fritzing sketch Schematic (saved by Fritzing 0.9.3b)
breadboards: 1

parts:
  Componente1 = Arduino Nano (Rev3.0)
  S1 = Round Pushbutton
  Componente2 = Breadboard Power Supply Board SMD
  Mod1 = KY-019 5V Relay Module [package="Breakout board"]
  R1 = Resistor [tolerance=±5% resistance=220 package="0603 [SMD]"]
  Mod2 = KY-016 RGB Full Color LED Module [package="Breakout board"]
  JP1 = Header 4 [package=molex-1x4_lock]

nets:
  GND: Componente1.GND, Componente2.GND, Mod1.-, R1.Pin_1, Mod2.-, JP1.3
  N1: Componente1.D5, S1.leg0, R1.Pin_0
  N2: Componente1.D6, Mod2.R
  N3: Componente1.D7, Mod2.G
  VIN: Componente1.VIN, S1.leg1, Componente2.VCC, Mod1.+, JP1.4
  N4: Componente1.A5, JP1.2
  N5: Componente1.A4, JP1.1

custom parts:
  KY-019 5V Relay Module: KY-019 5V Relay module, used to control AC circuits. (Special thanks to vanepp for fixing the PCB holes and other errors)
  KY-016 RGB Full Color LED Module: KY-016 Arduino full color 5mm RGB LED, different colors can be obtained by mixing the three primary colors.
